# Fritzing sketch plantifier_sketch_2 (saved by Fritzing 1.0.3b)
breadboards: 5

parts:
  Part1 = Soil Moisture Sensor
  Arduino_Nano = Arduino Nano (Rev3.0)
  LED1 = LED - 5mm [color="Red (633nm)" current=0.030A package="5 mm [THT]"]
  DHT1 = DHT11 Humitidy and Temperature Sensor
  R1 = Resistor [tolerance=±1% resistance=1k power=0.25W package="0805 [SMD]"]
  R2 = Resistor [tolerance=±0.5% resistance=1k power=0.25W package="1206 [SMD]"]
  Part3 = Soil Moisture Sensor
  Arduino_Nano2 = Arduino Nano (Rev3.0)
  DHT3 = DHT11 Humitidy and Temperature Sensor
  R5 = Resistor [tolerance=±1% resistance=1k power=0.25W package="0805 [SMD]"]
  R6 = Resistor [tolerance=±0.5% resistance=1k power=0.25W package="1206 [SMD]"]
  LED3 = LED - 5mm [color="Red (633nm)" current=0.030A package="5 mm [THT]"]

nets:
  VCC: Part1.VCC, Arduino_Nano.5V
  GND: Part1.GND, Arduino_Nano.GND, LED1.cathode, DHT1.GND
  N1: Part1.SIG, Arduino_Nano.A0
  N2: Arduino_Nano.D5, DHT1.DATA, R2.Pin_0
  N3: Arduino_Nano.D6, R1.Pin_1
  3V3: Arduino_Nano.3V3, DHT1.VDD, R2.Pin_1
  N4: LED1.anode, R1.Pin_0
  N5: Part3.SIG, Arduino_Nano2.A0
  GND_2: Part3.GND, Arduino_Nano2.GND, DHT3.GND, LED3.cathode
  VCC_2: Part3.VCC, Arduino_Nano2.5V
  N6: Arduino_Nano2.D5, DHT3.DATA, R6.Pin_0
  N7: Arduino_Nano2.D6, R5.Pin_1
  3V3_2: Arduino_Nano2.3V3, DHT3.VDD, R6.Pin_1
  N8: R5.Pin_0, LED3.anode

custom parts:
  DHT11 Humitidy and Temperature Sensor: DHT11 Humidity and Temperature Sensor
